# Fritzing sketch coeur (saved by Fritzing 0.9.3b)
breadboards: 1

parts:
  Composant1 = Arduino Uno (Rev3)
  LED1 = LED - 5mm [color="Red (633nm)" package="5 mm [THT]"]
  LED2 = LED - 5mm [color="Red (633nm)" package="5 mm [THT]"]
  LED3 = LED - 5mm [color="Red (633nm)" package="5 mm [THT]"]
  LED4 = LED - 5mm [color="Red (633nm)" package="5 mm [THT]"]
  LED5 = LED - 5mm [color="Red (633nm)" package="5 mm [THT]"]
  LED6 = LED - 5mm [color="Red (633nm)" package="5 mm [THT]"]
  LED7 = LED - 5mm [color="Red (633nm)" package="5 mm [THT]"]
  LED8 = LED - 5mm [color="Red (633nm)" package="5 mm [THT]"]
  R1 = Resistor [tolerance=±5% resistance=220 package="2512 [SMD]"]
  R2 = Resistor [tolerance=±5% resistance=220 package="2512 [SMD]"]
  R3 = Resistor [tolerance=±5% resistance=220 package="2512 [SMD]"]
  R4 = Resistor [tolerance=±5% resistance=220 package="2512 [SMD]"]
  R5 = Resistor [tolerance=±5% resistance=220 package="2512 [SMD]"]
  R6 = Resistor [tolerance=±5% resistance=220 package="2512 [SMD]"]
  R7 = Resistor [tolerance=±5% resistance=220 package="2512 [SMD]"]
  R8 = Resistor [tolerance=±5% resistance=220 package="2512 [SMD]"]

nets:
  N1: Composant1.D8, R6.Pin_0
  N2: Composant1.D9_PWM, R4.Pin_0
  N3: Composant1.D10_PWM/SS, R2.Pin_1
  N4: Composant1.D11_PWM/MOSI, R8.Pin_1
  N5: Composant1.D12/MISO, R5.Pin_1
  N6: Composant1.D13/SCK, R1.Pin_1
  N7: Composant1.D6_PWM, R7.Pin_1
  N8: Composant1.D7, R3.Pin_1
  N9: Composant1.5V, LED2.cathode
  N10: Composant1.GND, LED1.cathode, LED3.cathode, LED4.cathode, LED5.cathode, LED6.cathode, LED7.cathode, LED8.cathode
  N11: LED1.anode, R8.Pin_0
  N12: LED2.anode, R1.Pin_0
  N13: LED3.anode, R5.Pin_0
  N14: LED4.anode, R7.Pin_0
  N15: LED5.anode, R2.Pin_0
  N16: LED6.anode, R6.Pin_1
  N17: LED7.anode, R4.Pin_1
  N18: LED8.anode, R3.Pin_0
