# Fritzing sketch modèle_électronique_arduino_final (saved by Fritzing 0.9.3b)
breadboards: 2

parts:
  Composant1 = Arduino Uno (Rev3)
  R1 = Resistor [tolerance=±5% resistance=1k package=THT]
  D1 = LTE-302 [package=lte-302]
  U1 = LM124-324 Quad Opamp [package="DIP (Dual Inline)"]
  R2 = Resistor [tolerance=±5% resistance=68k package="1206 [SMD]"]
  C1 = Ceramic Capacitor [capacitance=1µF package="0805 [SMD, multilayer]"]
  R3 = Resistor [tolerance=±5% resistance=10k package="2010 [SMD]"]
  Q1 = LTR-301 [package=ltr-301]
  C2 = Ceramic Capacitor [capacitance=1µF package="0805 [SMD, multilayer]"]
  R4 = Resistor [tolerance=±5% resistance=8.2k package="1206 [SMD]"]
  C3 = Ceramic Capacitor [capacitance="100 nF" package="0805 [SMD, multilayer]"]
  C4 = Ceramic Capacitor [capacitance="100 nF" package="0805 [SMD, multilayer]"]
  R5 = Resistor [tolerance=±5% resistance=1k package="1206 [SMD]"]
  R6 = Resistor [tolerance=±5% resistance=470k package="1206 [SMD]"]
  R7 = Resistor [tolerance=±5% resistance=220 package="1206 [SMD]"]
  Q2 = NPN-Transistor [package="SOT-23 [SMD]"]
  R8 = Resistor [tolerance=±5% resistance=68k package=THT]
  R9 = Resistor [tolerance=±5% resistance=1k package="1206 [SMD]"]
  LED9 = LED - 5mm [color="Red (633nm)" package="5 mm [THT]"]
  LED10 = LED - 5mm [color="Red (633nm)" package="5 mm [THT]"]
  LED11 = LED - 5mm [color="Red (633nm)" package="5 mm [THT]"]
  LED12 = LED - 5mm [color="Red (633nm)" package="5 mm [THT]"]
  LED13 = LED - 5mm [color="Red (633nm)" package="5 mm [THT]"]
  LED14 = LED - 5mm [color="Red (633nm)" package="5 mm [THT]"]
  LED15 = LED - 5mm [color="Red (633nm)" package="5 mm [THT]"]
  R10 = Resistor [tolerance=±5% resistance=220 package="2512 [SMD]"]
  LED16 = LED - 5mm [color="Red (633nm)" package="5 mm [THT]"]
  R11 = Resistor [tolerance=±5% resistance=220 package="2512 [SMD]"]
  R12 = Resistor [tolerance=±5% resistance=220 package="2512 [SMD]"]
  R13 = Resistor [tolerance=±5% resistance=220 package="2512 [SMD]"]
  R14 = Resistor [tolerance=±5% resistance=220 package="2512 [SMD]"]
  R15 = Resistor [tolerance=±5% resistance=220 package="2512 [SMD]"]
  R16 = Resistor [tolerance=±5% resistance=220 package="2512 [SMD]"]
  R17 = Resistor [tolerance=±5% resistance=220 package="2512 [SMD]"]

nets:
  N1: Composant1.A0, Q2.2
  N2: Composant1.D8, R15.Pin_0
  N3: Composant1.D9_PWM, R13.Pin_0
  N4: Composant1.D10_PWM/SS, R11.Pin_1
  N5: Composant1.D11_PWM/MOSI, R17.Pin_1
  N6: Composant1.D12/MISO, R14.Pin_1
  N7: Composant1.D13/SCK, R10.Pin_1
  N8: Composant1.GND, D1.A, U1.VCC+, U1.2OUT, R2.Pin_0, Q1.E, R4.Pin_1, C4.0, R5.Pin_0, R6.Pin_1, R7.Pin_0, R8.Pin_0, R9.Pin_0, LED9.cathode, LED10.cathode, LED11.cathode, LED12.cathode, LED13.cathode, LED14.cathode, LED15.cathode
  N9: Composant1.D6_PWM, R16.Pin_1
  N10: Composant1.D7, R12.Pin_1
  N11: Composant1.5V, R1.Pin_1, U1.VCC-, R3.Pin_1, LED16.cathode
  N12: R1.Pin_0, D1.C
  N13: U1.2IN+, C3.1, R8.Pin_1
  N14: U1.2IN-, C4.1, R5.Pin_1, R6.Pin_0
  N15: U1.3OUT, C2.1, C3.0
  N16: U1.3IN-, R4.Pin_0
  N17: U1.3IN+, R2.Pin_1, C1.1, C2.0
  N18: C1.0, R3.Pin_0, Q1.C
  N19: R7.Pin_1, Q2.0
  N20: Q2.1, R9.Pin_1
  N21: LED9.anode, R17.Pin_0
  N22: LED10.anode, R14.Pin_0
  N23: LED11.anode, R16.Pin_0
  N24: LED12.anode, R12.Pin_0
  N25: LED13.anode, R15.Pin_1
  N26: LED14.anode, R11.Pin_0
  N27: LED15.anode, R13.Pin_1
  N28: R10.Pin_0, LED16.anode
